# Fritzing sketch fritz (saved by Fritzing 0.9.6b)
breadboards: 1

parts:
  Part1 = Arduino Uno (Rev3)
  R1 = Resistor [tolerance=±5% resistance=220 package="1206 [SMD]"]
  LED1 = RGB LED (com. anode, rbg) [package="5 mm [THT]"]
  J1 = Dagu DGServo 9g header (male) [package=THT]
  J5 = Dagu DGServo 9g header (male) [package=THT]
  U2 = Barometric Pressure Sensor
  J8 = Dagu DGServo 9g header (male) [package=THT]

nets:
  N1: Part1.A0, J8.analog
  N2: Part1.D8, J5.up
  N3: Part1.D9_PWM, LED1.green_cathode
  N4: Part1.D10_PWM/SS, LED1.common_anode
  N5: Part1.D11_PWM/MOSI, LED1.red_cathode
  N6: Part1.D12/MISO, J1.sel
  N7: Part1.D13/SCK, J1.st
  GND: Part1.GND, R1.Pin_0, J1.gnd, J5.gnd, U2.gnd, J8.gnd
  N8: Part1.D2, U2.green
  N9: Part1.D3_PWM, U2.red
  N10: Part1.D4, U2.yellow
  N11: Part1.D5_PWM, U2.blu
  N12: Part1.D6_PWM, U2.orange
  N13: Part1.D7, J5.dn
  5V: Part1.5V, J8.5v
  N14: R1.Pin_1, LED1.blue_cathode

custom parts:
  Dagu DGServo 9g header (male): Dagu DGServo 9g header (male) This part is a minor variation of the standard three pin header; in schematic view the pins have been labelled to show clearly pulse, Vcc and ground. Plug this header into a breadboard, stripboard or PCB to allow a servo header female connector plug (e.g. on the Dagu DGServo 9g) to be connected to the board.
  Dagu DGServo 9g header (male): Dagu DGServo 9g header (male) This part is a minor variation of the standard three pin header; in schematic view the pins have been labelled to show clearly pulse, Vcc and ground. Plug this header into a breadboard, stripboard or PCB to allow a servo header female connector plug (e.g. on the Dagu DGServo 9g) to be connected to the board.
  Barometric Pressure Sensor: SCP1000 Barometric Pressure sensor. Can sense air pressure and temperature. SPI interface.
  Dagu DGServo 9g header (male): Dagu DGServo 9g header (male) This part is a minor variation of the standard three pin header; in schematic view the pins have been labelled to show clearly pulse, Vcc and ground. Plug this header into a breadboard, stripboard or PCB to allow a servo header female connector plug (e.g. on the Dagu DGServo 9g) to be connected to the board.
